# Fritzing sketch RFID-Circuit (saved by Fritzing 0.9.3b)

parts:
  Part1 = RFID-RC522-v2
  Raspberry_Pi_1 = Raspberry Pi 3 [part_number=RPI-3-V1.2]

nets:
  N1: Part1.SDA, Raspberry_Pi_1.GIPO8
  N2: Part1.SCK, Raspberry_Pi_1.GIPO11
  N3: Part1.MOSI, Raspberry_Pi_1.GIPO10
  N4: Part1.MISO, Raspberry_Pi_1.GIPO9
  GND: Part1.GND, Raspberry_Pi_1.GND
  N5: Part1.RST, Raspberry_Pi_1.GIPO25
  3.3V: Part1.3.3V, Raspberry_Pi_1.3v3

notes:
  Connections
  Red = 3.3V = Pi 3.3V
  Grey = RST = GPIO25
  Black = GND = Any Pi GND
  Green = MISO = GPIO9
  White = MOSI = GPIO10
  Yellow = SCK = GPIO11
  Orange = SDA = GPIO8

custom parts:
  RFID-RC522-v2: A simple China made RFID-RC522 Reader; do check the pin labels, as this is a MFRC522 based clone.
